// Logisim project CPU.circ as structural Verilog: 5 circuits, main circuit cpu_main
module system (
  input  in_1
);

  wire ck, cs1, cs2;
  wire [3:0] cpu_main_1_cmd;
  wire [9:0] rom_adapter_1_rom_add;
  wire [31:0] cpu_main_1_address, cpu_main_1_dout, rom_1_data, rom_adapter_1_data;

  Clock clock_1 (.out(ck));
  ROM #(.addrWidth(10), .dataWidth(32)) rom_1 (.addr(rom_adapter_1_rom_add), .data(rom_1_data));
  RAM ram_1 ();  // open: addr, we, oe, clk, din, dout
  cpu_main cpu_main_1 (
    .\int (in_1), .CK(ck), .din(rom_adapter_1_data), .address(cpu_main_1_address), .dout(cpu_main_1_dout),
    .cmd(cpu_main_1_cmd));  // open: ready
  rom_adapter rom_adapter_1 (
    .address(cpu_main_1_address), .cmd(cpu_main_1_cmd), .rom_data(rom_1_data), .cs(cs1),
    .rom_add(rom_adapter_1_rom_add), .data(rom_adapter_1_data));
  // cs_memory cs_mem: pin names not known; wires that end beside it: cpu_main_1_dout, rom_adapter_1_data, cpu_main_1_cmd, cpu_main_1_address, cs1, cs2
  TTY #(.cols(48), .rows(12)) tty_1 ();  // open: data, clk, we, clr
  Keyboard keyboard_1 ();  // open: clk, re, clr, avail, data

  // Notes on the sheet:
  //   contents of rom_1 (hex, n*v repeats v):
  //   8010005
endmodule

module cpu_main (
  input  CK,
  input  \int ,
  input  ready,
  input  [31:0] din,
  output [31:0] address,
  output [31:0] dout,
  output [3:0] cmd
);

  wire udc_main_1_cost_enable, udc_main_1_rd1, udc_main_1_rd2, udc_main_1_wr;
  wire [4:0] udc_main_1_out_12, udc_main_1_out_14, udc_main_1_out_16;
  wire [31:0] udc_main_1_cost, udc_main_1_reg_ctrl;

  udc_main udc_main_1 (
    .INT(\int ), .ir_in(din), .CK(CK), .ready(ready), .cost_enable(udc_main_1_cost_enable),
    .cmd_signals(cmd), .reg_ctrl(udc_main_1_reg_ctrl), .RD1(udc_main_1_rd1), .out_12(udc_main_1_out_12),
    .RD2(udc_main_1_rd2), .out_14(udc_main_1_out_14), .WR(udc_main_1_wr), .out_16(udc_main_1_out_16),
    .COST(udc_main_1_cost));  // open: ZF, ask_ready, U, cond
  dp_main dp_main_1 (
    .WR(udc_main_1_wr), .c_en(udc_main_1_reg_ctrl[13:11]), .Waddr(udc_main_1_out_16),
    .addrMux(udc_main_1_reg_ctrl[30]), .cost_en(udc_main_1_cost_enable), .RD1(udc_main_1_rd1),
    .Raddr1(udc_main_1_out_12), .a_en(udc_main_1_reg_ctrl[7:5]), .b_en(udc_main_1_reg_ctrl[10:8]),
    .Raddr2(udc_main_1_out_14), .RD2(udc_main_1_rd2), .pc_en(udc_main_1_reg_ctrl[16:14]),
    .temp_en(udc_main_1_reg_ctrl[19:17]), .iar_en(udc_main_1_reg_ctrl[22:20]),
    .mar_en(udc_main_1_reg_ctrl[25:23]), .mdr_en(udc_main_1_reg_ctrl[28:26]), .cost_in(udc_main_1_cost),
    .alu_ctrl(udc_main_1_reg_ctrl[4:0]), .dataMux(udc_main_1_reg_ctrl[29]), .CK(CK), .data_in(din),
    .address_out(address), .data_out(dout));  // open: flags
endmodule

module cs_memory (
  input  [31:0] address,
  output cs_mem_1,
  output out_3,
  output out_4,
  output out_5,
  output out_6,
  output out_7,
  output out_8,
  output out_9,
  output out_10,
  output out_11,
  output out_12,
  output out_13,
  output out_14,
  output out_15,
  output out_16,
  output cs_mem_16
);

  Decoder #(.enable("false"), .select(4)) decoder_1 (
    .out0(cs_mem_1), .out1(out_3), .out2(out_4), .out3(out_5), .out4(out_6), .out5(out_7), .out6(out_8),
    .out7(out_9), .out8(out_10), .out9(out_11), .out10(out_12), .out11(out_13), .out12(out_14),
    .out13(out_15), .out14(out_16), .out15(cs_mem_16), .sel(address[13:10]));

  // Notes on the sheet:
  //   i=10
endmodule

module rom_adapter (
  input  cs,
  input  [3:0] cmd,
  input  [31:0] rom_data,
  input  [31:0] address,
  output [9:0] rom_add,
  output [31:0] data
);

  wire and_1_out;

  and and_1 (and_1_out, cs, cmd[0]);
  assign data = and_1_out ? rom_data : 32'bz;  // Controlled_Buffer controlled_buffer_1

  assign rom_add = address[9:0];

  // Notes on the sheet:
  //   memrd
endmodule

module memtest (
  input  [7:0] in_1,
  input  [7:0] in_2,
  output [7:0] LSB,
  output [7:0] out_4,
  output [7:0] out_5,
  output [7:0] MSB
);

  wire [7:0] adder_1_out, adder_2_out;

  // ROM #(.line("quad")) rom_1: pin names not known; wires that end beside it: in_1, LSB, out_4, out_5, MSB
  Adder adder_1 (.a(in_2), .b({8{1'b0}}), .out(adder_1_out), .cin(1'b1));  // open: cout
  Adder adder_2 (.a(adder_1_out), .b({8{1'b0}}), .out(adder_2_out), .cin(1'b1));  // open: cout
  RAM #(.asyncread("true")) ram_1 (.addr(in_2));  // open: we, oe, clk, din, dout
  RAM #(.asyncread("true")) ram_2 (.addr(adder_1_out));  // open: we, oe, clk, din, dout
  RAM #(.asyncread("true")) ram_3 (.addr(adder_2_out));  // open: we, oe, clk, din, dout
  RAM #(.asyncread("true")) ram_4 ();  // open: addr, we, oe, clk, din, dout

  // Notes on the sheet:
  //   contents of rom_1 (hex, n*v repeats v):
  //   af 80 0 1
endmodule
